// Logisim project retroputer.circ as structural Verilog: 5 circuits, main circuit main
module main (
);

  wire clock_1_out, comparator_1_eq, cpu_1_d_read, cpu_1_d_write, cpu_1_io_read, cpu_1_io_write,
       io_bus_1_irq_request, io_bus_1_rd_valid, reset_out;
  wire [7:0] cpu_1_d_out, cpu_1_io_out, cpu_1_io_port, io_bus_1_io_out, mem_dout, multiplexer_1_out,
       rom_1_data;
  wire [15:0] cpu_1_irq_ack, io_bus_1_irq;
  wire [18:0] cpu_1_address;

  Clock clock_1 (.out(clock_1_out));
  Button reset (.out(reset_out));
  RAM #(.addrWidth(19)) mem (
    .addr(cpu_1_address), .we(cpu_1_d_write), .oe(cpu_1_d_read), .clk(clock_1_out), .din(cpu_1_d_out),
    .dout(mem_dout));
  cpu cpu_1 (
    .clk(clock_1_out), .rst(reset_out), .trap(io_bus_1_irq_request), .irq(io_bus_1_irq),
    .d_in(multiplexer_1_out), .io_in(io_bus_1_io_out), .io_rdy(io_bus_1_rd_valid), .irq_ack(cpu_1_irq_ack),
    .address(cpu_1_address), .d_out(cpu_1_d_out), .d_read(cpu_1_d_read), .d_write(cpu_1_d_write),
    .io_port(cpu_1_io_port), .io_out(cpu_1_io_out), .io_read(cpu_1_io_read), .io_write(cpu_1_io_write));  // open: ready, d_rdy
  ROM #(.addrWidth(16)) rom_1 (.addr(cpu_1_address[15:0]), .data(rom_1_data));
  Comparator #(.width(3)) comparator_1 (.a(cpu_1_address[18:16]), .b(3'b111), .eq(comparator_1_eq));  // open: gt, lt
  Multiplexer #(.width(8)) multiplexer_1 (
    .in0(mem_dout), .in1(rom_1_data), .out(multiplexer_1_out), .sel(comparator_1_eq));
  io_bus io_bus_1 (
    .clk(clock_1_out), .rst(reset_out), .io_addr(cpu_1_io_port), .io_in(cpu_1_io_out),
    .io_read(cpu_1_io_read), .io_write(cpu_1_io_write), .irq_ack(cpu_1_irq_ack), .io_out(io_bus_1_io_out),
    .rd_valid(io_bus_1_rd_valid), .irq(io_bus_1_irq), .irq_request(io_bus_1_irq_request));  // open: device_in, device_rd_valid, device_irq_service, device_sel, rdy, device_port, device_out, device_read, device_write, device_irq_ack
endmodule

module cpu (
  input  clk,
  input  rst,
  input  trap,
  input  [15:0] irq,
  input  ready,
  input  [7:0] d_in,
  input  d_rdy,
  input  [7:0] io_in,
  input  io_rdy,
  output [15:0] irq_ack,
  output [18:0] address,
  output [7:0] d_out,
  output d_read,
  output d_write,
  output [7:0] io_port,
  output [7:0] io_out,
  output io_read,
  output io_write
);

  wire alu_1_carry, alu_1_negative, alu_1_overflow, alu_1_zero;
  wire [15:0] alu_1_result;

  alu alu_1 (
    .carry_in(1'b0), .a(16'h105), .size_a(1'b1), .b(16'h16f), .size_b(1'b1), .size_r(1'b1), .op(5'b00001),
    .carry(alu_1_carry), .zero(alu_1_zero), .negative(alu_1_negative), .result(alu_1_result),
    .overflow(alu_1_overflow));
  // Probe on alu_1_zero
  // Probe on alu_1_result
  // Probe on alu_1_carry
  // Probe on alu_1_negative
  // Probe on alu_1_overflow
endmodule

module alu (
  input  carry_in,
  input  [15:0] a,
  input  size_a,
  input  [15:0] b,
  input  size_b,
  input  size_r,
  input  [4:0] op,
  output carry,
  output zero,
  output negative,
  output [15:0] result,
  output overflow
);

  wire adder_1_cout, adder_2_cout, and_4_out, and_5_out, multiplexer_3_out, multiplexer_4_out,
       subtractor_1_bout, subtractor_2_bout, xnor_1_out, xor_2_out, xor_3_out, xor_4_out;
  wire [15:0] adder_1_out, adder_2_out, and_1_out, and_2_out, and_3_out, and_6_out, multiplexer_1_out,
       multiplexer_2_out, multiplexer_5_out, multiplier_1_out, negator_1_out, not_1_out, or_1_out,
       shifter_1_out, shifter_2_out, subtractor_1_out, subtractor_2_out, xor_1_out;

  assign and_1_out = 16'hff & a;  // AND_Gate and_1, 16 bits wide
  assign and_2_out = 16'hff & b;  // AND_Gate and_2, 16 bits wide
  Multiplexer #(.width(16)) multiplexer_1 (.in0(a), .in1(and_1_out), .out(multiplexer_1_out), .sel(size_a));
  Multiplexer #(.width(16)) multiplexer_2 (.in0(b), .in1(and_2_out), .out(multiplexer_2_out), .sel(size_b));
  Multiplexer multiplexer_3 (
    .in0(multiplexer_1_out[15]), .in1(multiplexer_1_out[7]), .out(multiplexer_3_out), .sel(size_a));
  Multiplexer multiplexer_4 (
    .in0(multiplexer_2_out[15]), .in1(multiplexer_2_out[7]), .out(multiplexer_4_out), .sel(size_b));
  assign not_1_out = ~multiplexer_1_out;  // NOT_Gate not_1, 16 bits wide
  Adder #(.width(16)) adder_1 (
    .a(multiplexer_1_out), .b(multiplexer_2_out), .out(adder_1_out), .cin(carry_in), .cout(adder_1_cout));
  Subtractor #(.width(16)) subtractor_1 (
    .a(multiplexer_1_out), .b(multiplexer_2_out), .out(subtractor_1_out), .bin(carry_in),
    .bout(subtractor_1_bout));
  Multiplier #(.width(16)) multiplier_1 (
    .a(multiplexer_1_out), .b(multiplexer_2_out), .out(multiplier_1_out));  // open: cin, cout
  Shifter #(.width(16)) shifter_1 (.in(multiplexer_1_out), .\dist (multiplexer_2_out[3:0]), .out(shifter_1_out));
  Shifter #(.shift("lr"), .width(16)) shifter_2 (
    .in(multiplexer_1_out), .\dist (multiplexer_2_out[3:0]), .out(shifter_2_out));
  assign and_3_out = multiplexer_1_out & multiplexer_2_out;  // AND_Gate and_3, 16 bits wide
  assign or_1_out = multiplexer_1_out | multiplexer_2_out;  // OR_Gate or_1, 16 bits wide
  assign xor_1_out = multiplexer_1_out ^ multiplexer_2_out;  // XOR_Gate xor_1, 16 bits wide
  Adder #(.width(16)) adder_2 (.a(multiplexer_1_out), .b(16'h1), .out(adder_2_out), .cin(1'b0), .cout(adder_2_cout));
  Subtractor #(.width(16)) subtractor_2 (
    .a(multiplexer_1_out), .b(16'h1), .out(subtractor_2_out), .bin(1'b0), .bout(subtractor_2_bout));
  xnor xnor_1 (xnor_1_out, multiplexer_3_out, multiplexer_4_out);
  xor xor_2 (xor_2_out, multiplexer_3_out, multiplexer_4_out);
  Negator #(.width(16)) negator_1 (.in(multiplexer_1_out), .out(negator_1_out));
  xor xor_3 (xor_3_out, multiplexer_3_out, negative);
  and and_4 (and_4_out, xnor_1_out, xor_3_out);
  xor xor_4 (xor_4_out, multiplexer_3_out, negative);
  Multiplexer #(.select(5), .width(16)) multiplexer_5 (
    .in0({16{1'b0}}), .in1(adder_1_out), .in2(subtractor_1_out), .in3(multiplier_1_out), .in4({16{1'b0}}),
    .in5({16{1'b0}}), .in6({16{1'b0}}), .in7({16{1'b0}}), .in8({16{1'b0}}), .in9(negator_1_out),
    .in10(shifter_1_out), .in11(shifter_2_out), .in12(and_3_out), .in13(or_1_out), .in14(xor_1_out),
    .in15(not_1_out), .in16(adder_2_out), .in17(subtractor_2_out), .in18({16{1'b0}}), .in19({16{1'b0}}),
    .in20({16{1'b0}}), .in21({16{1'b0}}), .in22({16{1'b0}}), .in23({16{1'b0}}), .in24({16{1'b0}}),
    .in25({16{1'b0}}), .in26({16{1'b0}}), .in27({16{1'b0}}), .in28({16{1'b0}}), .in29({16{1'b0}}),
    .in30({16{1'b0}}), .in31({16{1'b0}}), .out(multiplexer_5_out), .sel(op));
  and and_5 (and_5_out, xor_2_out, xor_4_out);
  Multiplexer #(.select(5)) multiplexer_6 (
    .in0(1'b0), .in1(adder_1_cout), .in2(subtractor_1_bout), .in3(1'b0), .in4(1'b0), .in5(1'b0), .in6(1'b0),
    .in7(1'b0), .in8(1'b0), .in9(1'b0), .in10(1'b0), .in11(1'b0), .in12(1'b0), .in13(1'b0), .in14(1'b0),
    .in15(1'b0), .in16(adder_2_cout), .in17(subtractor_2_bout), .in18(1'b0), .in19(1'b0), .in20(1'b0),
    .in21(1'b0), .in22(1'b0), .in23(1'b0), .in24(1'b0), .in25(1'b0), .in26(1'b0), .in27(1'b0), .in28(1'b0),
    .in29(1'b0), .in30(1'b0), .in31(1'b0), .out(carry), .sel(op));
  assign and_6_out = 16'hff & multiplexer_5_out;  // AND_Gate and_6, 16 bits wide
  Multiplexer #(.width(16)) multiplexer_7 (.in0(multiplexer_5_out), .in1(and_6_out), .out(result), .sel(size_r));
  Multiplexer #(.select(5)) multiplexer_8 (
    .in0(1'b0), .in1(and_4_out), .in2(and_5_out), .in3(and_4_out), .in4(1'b0), .in5(1'b0), .in6(1'b0),
    .in7(1'b0), .in8(1'b0), .in9(1'b0), .in10(1'b0), .in11(1'b0), .in12(1'b0), .in13(1'b0), .in14(1'b0),
    .in15(1'b0), .in16(1'b0), .in17(1'b0), .in18(1'b0), .in19(1'b0), .in20(1'b0), .in21(1'b0), .in22(1'b0),
    .in23(1'b0), .in24(1'b0), .in25(1'b0), .in26(1'b0), .in27(1'b0), .in28(1'b0), .in29(1'b0), .in30(1'b0),
    .in31(1'b0), .out(overflow), .sel(op));
  Comparator #(.width(16)) comparator_1 (.a(multiplexer_5_out), .b({16{1'b0}}), .eq(zero));  // open: gt, lt
  Multiplexer multiplexer_9 (.in0(result[15]), .in1(result[7]), .out(negative), .sel(size_r));
endmodule

module io_bus (
  input  clk,
  input  rst,
  input  [7:0] io_addr,
  input  [7:0] io_in,
  input  io_read,
  input  [7:0] device_in,
  input  io_write,
  input  [15:0] irq_ack,
  input  device_rd_valid,
  input  device_irq_service,
  output [3:0] device_sel,
  output rdy,
  output [3:0] device_port,
  output [7:0] io_out,
  output [7:0] device_out,
  output rd_valid,
  output device_read,
  output device_write,
  output [15:0] irq,
  output irq_request,
  output device_irq_ack
);

  wire comparator_1_eq;

  Comparator #(.width(16)) comparator_1 (.a(irq), .b({16{1'b0}}), .eq(comparator_1_eq));  // open: gt, lt
  not not_1 (irq_request, comparator_1_eq);
  Decoder #(.select(4)) decoder_1 (
    .out0(irq[0]), .out1(irq[1]), .out2(irq[2]), .out3(irq[3]), .out4(irq[4]), .out5(irq[5]), .out6(irq[6]),
    .out7(irq[7]), .out8(irq[8]), .out9(irq[9]), .out10(irq[10]), .out11(irq[11]), .out12(irq[12]),
    .out13(irq[13]), .out14(irq[14]), .out15(irq[15]), .sel(io_addr[7:4]), .en(device_irq_service));
  Multiplexer #(.select(4)) multiplexer_1 (
    .in0(irq_ack[0]), .in1(irq_ack[1]), .in2(irq_ack[2]), .in3(irq_ack[3]), .in4(irq_ack[4]),
    .in5(irq_ack[5]), .in6(irq_ack[6]), .in7(irq_ack[7]), .in8(irq_ack[8]), .in9(irq_ack[9]),
    .in10(irq_ack[10]), .in11(irq_ack[11]), .in12(irq_ack[12]), .in13(irq_ack[13]), .in14(irq_ack[14]),
    .in15(irq_ack[15]), .out(device_irq_ack), .sel(io_addr[7:4]));

  assign device_out = io_in;
  assign device_port = io_addr[3:0];
  assign device_read = io_read;
  assign device_sel = io_addr[7:4];
  assign device_write = io_write;
  assign io_out = device_in;
  assign rd_valid = device_rd_valid;

  // Other names for the same wires on the sheet: io_addr_tnl[7:0] = io_addr; io_in_tnl[7:0] = io_in;
  //   io_out_tnl[7:0] = device_in; io_read_tnl = io_read; io_write_tnl = io_write; irq_ack_tnl[15:0] = irq_ack;
  //   irq_tnl[15:0] = irq; rd_valid_tnl = device_rd_valid
endmodule

module device_0_timer (
  input  clk,
  input  rst,
  input  [3:0] device_sel,
  input  [3:0] device_port,
  input  [7:0] device_data_in,
  input  device_read,
  input  device_write,
  input  device_irq_ack,
  output [7:0] device_data_out,
  output device_rd_valid,
  output device_irq_service,
  output device_wr_rdy
);

  wire counter_1_carry, rtc_1_min_carry, rtc_2_sec_carry, rtc_3_cent_carry, selected;

  Counter #(.max('h17)) rtc_0_hr (.count(rtc_1_min_carry), .clk(clk), .clr(rst));  // open: load, D, Q, carry, up
  Counter #(.max('h3d)) rtc_1_min (
    .count(rtc_2_sec_carry), .carry(rtc_1_min_carry), .clk(clk), .clr(rst));  // open: load, D, Q, up
  Comparator #(.width(4)) comparator_1 (.a(device_sel), .b(4'b0001), .eq(selected));  // open: gt, lt
  Counter #(.max('h3d)) rtc_2_sec (
    .count(rtc_3_cent_carry), .carry(rtc_2_sec_carry), .clk(clk), .clr(rst));  // open: load, D, Q, up
  Register temp_0 (.clr(rst));  // open: D, en, clk, Q
  Counter #(.max('h63)) rtc_3_cent (
    .count(counter_1_carry), .carry(rtc_3_cent_carry), .clk(clk), .clr(rst));  // open: load, D, Q, up
  Counter #(.max('h23), .width(20)) counter_1 (
    .clr(rst), .up(clk), .clk(clk), .carry(counter_1_carry));  // open: load, count, D, Q
endmodule
